// Logisim project lab41_somador_completo.circ as structural Verilog: 1 circuit, main circuit main
module main (
  input  A,
  input  B,
  input  CIN,
  output SOMA,
  output COUT
);

  wire and_1_out, and_2_p3, xor_1_p3;

  // XOR_Gate xor_1: pin names not known; wires that end beside it: A, B, xor_1_p3
  and and_1 (and_1_out, A, B);
  // XOR_Gate xor_2: pin names not known; wires that end beside it: xor_1_p3, CIN, SOMA
  // AND_Gate and_2: pin names not known; wires that end beside it: xor_1_p3, CIN, and_2_p3
  or or_1 (COUT, and_1_out, and_2_p3);

  // Notes on the sheet:
  //   Somador completo: SOMA = A^B^CIN, COUT = A.B + (A^B).CIN
endmodule
