// Logisim project meio_somador.circ as structural Verilog: 1 circuit, main circuit main
module main (
  input  A,
  input  B,
  output SOMA,
  output CARRY
);

  // XOR_Gate xor_1: pin names not known; wires that end beside it: A, B, SOMA
  and and_1 (CARRY, A, B);

  // Notes on the sheet:
  //   Meio somador: SOMA = A XOR B, CARRY = A AND B
endmodule
