// Logisim project portas_basicas.circ as structural Verilog: 1 circuit, main circuit main
module main (
  input  A_AND,
  input  B_AND,
  input  A_OR,
  input  B_OR,
  input  A_XOR,
  input  B_XOR,
  input  A_NAND,
  input  B_NAND,
  input  A_NOR,
  input  B_NOR,
  input  A_XNOR,
  input  B_XNOR,
  output AND,
  output OR,
  output XOR,
  output NAND,
  output NOR,
  output XNOR
);

  and and_1 (AND, A_AND, B_AND);
  or or_1 (OR, A_OR, B_OR);
  // XOR_Gate xor_1: pin names not known; wires that end beside it: A_XOR, B_XOR, A_NAND, XOR
  // NAND_Gate nand_1: pin names not known; wires that end beside it: B_XOR, A_NAND, B_NAND, A_NOR, NAND
  // NOR_Gate nor_1: pin names not known; wires that end beside it: B_NAND, A_NOR, B_NOR, A_XNOR, NOR
  // XNOR_Gate xnor_1: pin names not known; wires that end beside it: B_NOR, A_XNOR, B_XNOR, XNOR

  // Notes on the sheet:
  //   Portas basicas: clique nos pins de entrada (A e B) com a Poke Tool
endmodule
