// Logisim project ex01_tabelas.circ as structural Verilog: 1 circuit, main circuit main
module main (
  input  A,
  input  B,
  output AND,
  output OR,
  output XOR,
  output NOT_A
);


  // Notes on the sheet:
  //   Ex 1: monte AND, OR, XOR e NOT ligando A e B as saidas
endmodule
