// Logisim project ex02_a_and_b_or_c.circ as structural Verilog: 1 circuit, main circuit main
module main (
  input  A,
  input  B,
  input  C,
  output F
);


  // Notes on the sheet:
  //   Ex 2: F = A AND (B OR C)
endmodule
