// Logisim project ex03_xor_sem_xor.circ as structural Verilog: 1 circuit, main circuit main
module main (
  input  A,
  input  B,
  output XOR_NATIVO,
  output XOR_MONTADO
);


  // Notes on the sheet:
  //   Ex 3: monte XOR so com AND/OR/NOT e compare com a porta XOR nativa
endmodule
