// Logisim project ex05_meio_somador.circ as structural Verilog: 1 circuit, main circuit main
module main (
  input  A,
  input  B,
  output SOMA,
  output CARRY
);


  // Notes on the sheet:
  //   Ex 5: meio somador (A, B -> SOMA, CARRY)
endmodule
