// Logisim project ex06_flipflop_d.circ as structural Verilog: 1 circuit, main circuit main
module main (
  input  D,
  input  CLK,
  output Q
);


  // Notes on the sheet:
  //   Ex 6: flip-flop D (use o componente D Flip-Flop e observe Q so mudar na borda do clock)
endmodule
