// Logisim project ex07_trava_senha.circ as structural Verilog: 1 circuit, main circuit main
module main (
  input  [3:0] DIGITO,
  input  CLK,
  input  RESET,
  output ABRE
);


  // Notes on the sheet:
  //   Ex 7: trava com senha 8-1-5-3. DIGITO (4 bits) a cada pulso de CLK; ABRE=1 so se a sequencia estiver certa
endmodule
