// Logisim project lab37_portas.circ as structural Verilog: 1 circuit, main circuit main
module main (
  input  A,
  input  B,
  output ORIGINAL,
  output SIMPLIFICADA
);


  // Notes on the sheet:
  //   Lab 37: De Morgan - monte NOT(A AND B) e a forma simplificada (so OR e NOT); as saidas devem ser iguais
endmodule
