// Logisim project lab38_tabelas_verdade.circ as structural Verilog: 1 circuit, main circuit main
module main (
  input  A,
  input  B,
  input  C,
  output F
);


  // Notes on the sheet:
  //   Lab 38: F = (A XOR B) OR (A AND C); confira com Window > Combinational Analysis
endmodule
