// Logisim project lab39_multiplexador.circ as structural Verilog: 1 circuit, main circuit main
module main (
  input  D0,
  input  D1,
  input  S,
  output Y
);


  // Notes on the sheet:
  //   Lab 39: MUX 2x1 com portas: Y = (NOT S AND D0) OR (S AND D1)
endmodule
