// Logisim project lab40_meio_somador.circ as structural Verilog: 1 circuit, main circuit main
module main (
  input  A,
  input  B,
  output SOMA,
  output CARRY
);


  // Notes on the sheet:
  //   Lab 40: meio somador
endmodule
