// Logisim project lab41_somador_4bits.circ as structural Verilog: 1 circuit, main circuit main
module main (
  input  A3,
  input  A2,
  input  A1,
  input  A0,
  input  B3,
  input  B2,
  input  B1,
  input  B0,
  input  CIN,
  output S3,
  output S2,
  output S1,
  output S0,
  output COUT
);


  // Notes on the sheet:
  //   Lab 41: somador de 4 bits encadeando 4 somadores completos
endmodule
