// Logisim project lab41_somador_completo.circ as structural Verilog: 1 circuit, main circuit main
module main (
  input  A,
  input  B,
  input  CIN,
  output SOMA,
  output COUT
);


  // Notes on the sheet:
  //   Lab 41: somador completo (A, B, CIN -> SOMA, COUT)
endmodule
