// Logisim project lab42_registrador.circ as structural Verilog: 1 circuit, main circuit main
module main (
  input  D3,
  input  D2,
  input  D1,
  input  D0,
  input  LOAD,
  input  CLK,
  output Q3,
  output Q2,
  output Q1,
  output Q0
);


  // Notes on the sheet:
  //   Lab 42: registrador de 4 bits com LOAD (carrega D na borda do clock quando LOAD=1)
endmodule
