// Logisim project lab43_contador.circ as structural Verilog: 1 circuit, main circuit main
module main (
  input  CLK,
  input  RESET,
  output Q2,
  output Q1,
  output Q0
);


  // Notes on the sheet:
  //   Lab 43: contador binario de 3 bits (000 a 111) com RESET
endmodule
