// Logisim project lab44_maquina_estados.circ as structural Verilog: 1 circuit, main circuit main
module main (
  input  X,
  input  CLK,
  input  RESET,
  output Z
);


  // Notes on the sheet:
  //   Lab 44: maquina de estados (defina estados, transicoes e a saida Z)
endmodule
